# Fritzing sketch duemilanove_vusb_and_eeprom (saved by Fritzing 0.4.3b)
breadboards: 1

parts:
  R1 = Resistor [resistance=68 package=THT]
  D1 = Zener Diode [package="300 mil [THT]"]
  LEDR = Red LED - 5mm
  R6 = Resistor [resistance=470 package=THT]
  R5 = Resistor [resistance=470 package=THT]
  R4 = Resistor [resistance=470 package=THT]
  LEDY = yellow LED - 5mm
  LEDG = green LED - 5mm
  D2 = Zener Diode [package="300 mil [THT]"]
  R2 = Resistor [resistance=68 package=THT]
  R3 = Resistor [resistance=2.2k package=THT]
  CONN1 = USB connector [package=THT]
  IC1 = 24LC512 [package=THT]
  R7 = Resistor [resistance=10k package=THT]
  R8 = Resistor [resistance=10k package=THT]
  Arduino1 = Arduino

nets:
  N1: R1.Pin_0, Arduino1.D4
  N2: R1.Pin_1, D1.cathode, CONN1.d+
  GND: D1.anode, LEDR.cathode, LEDY.cathode, LEDG.cathode, D2.anode, CONN1.GND, CONN1.chassis5, CONN1.chassis6, IC1.A0, IC1.A1, IC1.A2, IC1.0V, IC1.WP_-_Write_Protect, Arduino1.GND
  N3: LEDR.anode, R5.Pin_1
  N4: R6.Pin_0, CONN1.5V
  N5: R6.Pin_1, LEDY.anode
  N6: R5.Pin_0, Arduino1.D9
  N7: R4.Pin_0, Arduino1.D8
  N8: R4.Pin_1, LEDG.anode
  N9: D2.cathode, R2.Pin_1, R3.Pin_0, CONN1.d-
  N10: R2.Pin_0, Arduino1.D2
  N11: R3.Pin_1, Arduino1.D5
  N12: IC1.SDA_-_I2C_Data, R8.Pin_0, Arduino1.A4
  N13: IC1.SCL_-_I2C_Clock, R7.Pin_0, Arduino1.A5
  N14: IC1.+V, R7.Pin_1, R8.Pin_1, Arduino1.+5V

notes:
  D+
  D-
  +5v
  R1,2 68Ω
  R3 2.2KΩ
  R4,5,6 480Ω
  R7,8 10kΩ
  D1,2 3.6v 0.5w
