# Fritzing sketch 328p_with_usb_and_eeprom (saved by Fritzing 0.4.3b)
breadboards: 1

parts:
  R1 = Resistor [resistance=68 package=THT]
  D1 = Zener Diode [package="300 mil [THT]"]
  LEDR = Red LED - 5mm
  R6 = Resistor [resistance=470 package=THT]
  R5 = Resistor [resistance=470 package=THT]
  R4 = Resistor [resistance=470 package=THT]
  LEDY = yellow LED - 5mm
  LEDG = green LED - 5mm
  D2 = Zener Diode [package="300 mil [THT]"]
  R2 = Resistor [resistance=68 package=THT]
  R3 = Resistor [resistance=2.2k package=THT]
  IC1 = 24LC512 [package=THT]
  R7 = Resistor [resistance=10k package=THT]
  R8 = Resistor [resistance=10k package=THT]
  U1 = atmega168 [package="DIP28 [THT]"]
  S1 = Pushbutton [package="[THT]"]
  XTAL1 = Crystal [package=THT]
  C1 = Ceramic Disk Capacitor [package=THT]
  C2 = Ceramic Disk Capacitor [package=THT]
  R9 = Resistor [resistance=10k package=THT]
  CONN1 = USB connector [package=THT]

nets:
  N1: R1.Pin_0, U1.Pin_6
  N2: R1.Pin_1, D1.cathode, CONN1.d+
  GND: D1.anode, LEDR.cathode, LEDY.cathode, LEDG.cathode, D2.anode, IC1.A0, IC1.A1, IC1.A2, IC1.0V, IC1.WP_-_Write_Protect, U1.Pin_8, U1.Pin_22, S1.Pin_1, S1.Pin_2, C1.pin_0, C2.pin_1, CONN1.GND, CONN1.chassis5, CONN1.chassis6
  N3: LEDR.anode, R5.Pin_1
  N4: R6.Pin_0, IC1.+V, R7.Pin_1, R8.Pin_1, U1.Pin_7, U1.Pin_20, R9.Pin_1, CONN1.5V
  N5: R6.Pin_1, LEDY.anode
  N6: R5.Pin_0, U1.Pin_15
  N7: R4.Pin_0, U1.Pin_14
  N8: R4.Pin_1, LEDG.anode
  N9: D2.cathode, R2.Pin_1, R3.Pin_0, CONN1.d-
  N10: R2.Pin_0, U1.Pin_4
  N11: R3.Pin_1, U1.Pin_11
  N12: IC1.SDA_-_I2C_Data, R8.Pin_0, U1.Pin_27
  N13: IC1.SCL_-_I2C_Clock, R7.Pin_0, U1.Pin_28
  N14: U1.Pin_1, S1.Pin_3, S1.Pin_4, R9.Pin_0
  N15: U1.Pin_12, XTAL1.pin_0, C1.pin_1
  N16: U1.Pin_13, XTAL1.pin_1, C2.pin_0

notes:
  D+
  D-
  +5v
  R1,2 68Ω
  R3 2.2KΩ
  R4,5,6 480Ω
  R7,8,9 10kΩ
  D1,2 3.6v 0.5w
